# Fritzing sketch schema (saved by Fritzing 0.9.3b)
circuit board: 10.1482cm x 5.94244cm
breadboards: 1

parts:
  Part1 = Arduino Uno (Rev3)
  Dot_Matrix1 = LED Dot Matrix 18mm (0.7 INCH)
  U1 = 74HC595 SMD [package="SO16 [SMD]"]
  U2 = 74HC595 SMD [package="SO16 [SMD]"]

nets:
  N1: Part1.D2, U1.SH_CP
  N2: Part1.D3_PWM, U2.SH_CP
  N3: Part1.D4, U1.ST_CP
  N4: Part1.D5_PWM, U2.ST_CP
  N5: Part1.D6_PWM, U1.DS
  N6: Part1.D7, U2.DS
  N7: Dot_Matrix1.Column_1, U2.Q0
  N8: Dot_Matrix1.Row_3, U1.Q4
  N9: Dot_Matrix1.Column_2, U2.Q1
  N10: Dot_Matrix1.Row_5, U1.Q2
  N11: Dot_Matrix1.Row_6, U1.Q1
  N12: Dot_Matrix1.Row_7, U1.Q0
  N13: Dot_Matrix1.Column_4, U2.Q3
  N14: Dot_Matrix1.Column_5, U2.Q4
  N15: Dot_Matrix1.Row_4, U1.Q3
  N16: Dot_Matrix1.Column_3, U2.Q2
  N17: Dot_Matrix1.Row_2, U1.Q5
  N18: Dot_Matrix1.Row_1, U1.Q6
  5V: U1.MR, U2.MR, U2.VCC
  GND: U1.OE, U2.GND, U2.OE

// code stored in the sketch: exampleCode.ino
struct MatrixDisplayController {
  int firLatch = 2;//ROW
  int firClock = 4;
  int firData = 6;
  int secLatch = 3;//COL
  int secClock = 5;
  int secData = 7;

  byte colIndex = 0;

  byte data[7];

  void init() {
    pinMode(firLatch, OUTPUT);
    pinMode(firClock, OUTPUT);
    pinMode(firData, OUTPUT);
    pinMode(secLatch, OUTPUT);
    pinMode(secClock, OUTPUT);
    pinMode(secData, OUTPUT);
  }

  void draw() {
    digitalWrite(firLatch, LOW);
    digitalWrite(secLatch, LOW);
    //shiftOut(secData, secClock, MSBFIRST, );
    shiftOut(firData, firClock, MSBFIRST, data[colIndex]);
    shiftOut(secData, secClock, MSBFIRST, (B00000001 << colIndex) ^ B11111111);
    
    digitalWrite(firLatch, HIGH);
    digitalWrite(secLatch, HIGH);
    colIndex++;
    if(colIndex == 7){
      colIndex = 0;
    }
  }

  void clear() {
    data[0] = 0;
    data[1] = 0;
    data[2] = 0;
    data[3] = 0;
    data[4] = 0;
    data[5] = 0;
    data[6] = 0;
  }

  void setPixel(byte row, byte col, boolean on) {
    if (on) {
      byte d = data[col];
      bitSet( d, row);
      data[col] = d;
    } else {
      bitSet(row, data[col]);
    }

  }

};


MatrixDisplayController c;

void setup() {
  
  c.init();
  for(int x = 0; x < 5;x++){
      for(int y = 0; y < 7;y++){
      c.setPixel(x,y, (x+y) % 2 == 0);
    }
  }
  

}

void loop() {
  c.draw();
  delay(500);
}
